# Fritzing sketch PiezoServo (saved by Fritzing 0.9.2b)

parts:
  Battery9v = Battery block 9V
  Servo = Basic Servo
  PiezoSensor = Piezo Speaker
  ArduinoMegaExt = Arduino Mega 2560 (Rev3)
  R1 = Resistor [tolerance=±5% resistance=1M package=THT]

nets:
  GND: Battery9v.-, Servo.gnd, PiezoSensor.pin2, ArduinoMegaExt.GND, R1.Pin_1
  N1: Battery9v.+, ArduinoMegaExt.VIN
  VCC: Servo.vcc, ArduinoMegaExt.5V
  N2: Servo.pulse, ArduinoMegaExt.D3_PWM
  N3: PiezoSensor.pin1, ArduinoMegaExt.A10, R1.Pin_0
